# Fritzing sketch myWattmetre (saved by Fritzing 0.9.3b)
circuit board: 4cm x 9cm
breadboards: 1

parts:
  R2 = Resistor [tolerance=±5% resistance=2.2k package=THT]
  R20 = Resistor [tolerance=±5% resistance=10k package=THT]
  R17 = Resistor [tolerance=±5% resistance=10k package=THT]
  C6 = Ceramic Capacitor [capacitance=0.22mF voltage=10V package="100 mil [THT, multilayer]"]
  S3 = Screw terminal - 2 pins [package=THT]
  HLK-PM1 = HLK-PM01
  M-ADS1115 = Adafruit ADS1115 16Bit I2C ADC [part_number="Adafruit #1085"]
  R15 = Resistor [tolerance=±5% resistance=10k package=THT]
  U5 = ESP-12F (ESP8266 WiFi Module) [part_number=ESP8266]
  U8 = DIODE-ZENER [package=diode-zener]
  S4 = Screw terminal - 2 pins [package=THT]
  R22 = Resistor [tolerance=±5% resistance=10k package=THT]
  U2 = DIODE-ZENER [package=diode-zener]
  C3 = Ceramic Capacitor [capacitance=100nF package="100 mil [THT, multilayer]"]
  R14 = Resistor [tolerance=±5% resistance=10k package=THT]
  R21 = Resistor [tolerance=±5% resistance=10k package=THT]
  R16 = Resistor [tolerance=±5% resistance=10k package=THT]
  R23 = Resistor [tolerance=±5% resistance=10k package=THT]
  U6 = DIODE-ZENER [package=diode-zener]
  F2 = Resettable Fuse PTC [package=ptc]
  F1 = Resettable Fuse PTC [package=ptc]
  R19 = Resistor [tolerance=±5% resistance=10k package=THT]
  S2 = Screw terminal - 2 pins [package=THT]
  R5 = Resistor [tolerance=±5% resistance=10k package=THT]
  J-PRG = screw terminal, 5 pins
  S1 = Screw terminal - 2 pins [package=THT]
  J-AC = screw terminal, 2 pins
  U7 = DIODE-ZENER [package=diode-zener]
  R24 = Resistor [tolerance=±5% resistance=10k package=THT]
  R18 = Resistor [tolerance=±5% resistance=10k package=THT]
  C5 = Ceramic Capacitor [capacitance=100nF package="100 mil [THT, multilayer]"]
  C2 = Electrolytic Capacitor [capacitance=0.1nF package="100 mil [THT, electrolytic]"]
  R3 = Resistor [tolerance=±5% resistance=2.2k package=THT]

nets:
  GND: R2.Pin_0, C6.0, HLK-PM1.-Vo, M-ADS1115.GND, U5.GND, U5.GPIO15, U8.A, U2.A, C3.0, U6.A, J-PRG.pin5, U7.A, C5.0, C2.-
  1.5V: R2.Pin_1, R20.Pin_0, S3.pin1, R15.Pin_0, S4.pin1, R22.Pin_0, C3.1, S2.pin1, S1.pin1, R18.Pin_0, R3.Pin_1
  N1: R20.Pin_1, S3.pin2, R19.Pin_0
  N2: R17.Pin_0, S2.pin2, R18.Pin_1
  N3: R17.Pin_1, M-ADS1115.AIN1, U7.C
  3.3V: C6.1, HLK-PM1.+Vo, M-ADS1115.VDD, U5.VCC, U5.EN, R16.Pin_1, R23.Pin_1, R5.Pin_1, R24.Pin_1, C5.1, C2.+, R3.Pin_0
  N4: HLK-PM1.AC#0, F2.2, F1.1
  N5: HLK-PM1.AC#1, F1.2, J-AC.pin1
  N6: M-ADS1115.AIN3, U2.C, R21.Pin_1
  N7: M-ADS1115.AIN2, U6.C, R19.Pin_1
  N8: M-ADS1115.AIN0, U8.C, R14.Pin_1
  N9: M-ADS1115.SDA, U5.GPIO4, R5.Pin_0
  N10: M-ADS1115.SCL, U5.GPIO2, R23.Pin_0
  N11: R15.Pin_1, R14.Pin_0, S1.pin2
  N12: U5.RXD0, J-PRG.pin3
  DTR: U5.GPIO0, J-PRG.pin1, R24.Pin_0
  N13: U5.TXD0, J-PRG.pin2
  RST: U5.RST, R16.Pin_0, J-PRG.pin4
  N14: S4.pin2, R22.Pin_1, R21.Pin_0
  N15: F2.1, J-AC.pin2

notes:
  AC

custom parts:
  HLK-PM01: AC-DC 220V to 5V Step-Down Power Supply Module
  Adafruit ADS1115 16Bit I2C ADC: For microcontrollers without an analog-to-digital converter or when you want a higher-precision ADC, the ADS1115 provides 16-bit precision at 860 samples/second over I2C. The chip can be configured as 4 single-ended input channels, or two differential channels. As a nice bonus, it even includes a programmable gain amplifier, up to x16, to help boost up smaller single/differential signals to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
  ESP-12F (ESP8266 WiFi Module): WiFi Module based on the ESP8266 with onboard PCB antenna and UART communications
